# Fritzing sketch Schematic (saved by Fritzing 0.9.10b)
breadboards: 1

parts:
  Mod1 = OLED Mono 0.56 inch blue or white
  WeMos_D1_Mini1 = WeMos D1 Mini
  U2 = RELAY [package=relay-t9a-2]  # not connected
  U3 = LIPO-2000mAh [package=lipo-2000]
  DC1 = DC_DC_XL4016 [part_number=8V package=board_screw]  # not connected
  ChargePort = Camdenboss CTB0158-2 [part_number=CTB0158-2 package=THT]
  M1 = INA3221 Triple Channel Current/Voltage Monitor Module [part_number="3221 Black"]
  Q1 = Basic FET N-Channel [package="DPak [SMD]"]
  R1 = Resistor [tolerance=±5% power=0.25 resistance=10k package=THT]
  D1 = Zener Diode [part_number=30SQ050 breakdown_voltage=3.6V package="300 mil [THT]"]
  U4 = RELAY [package=relay-t9a-2]
  U5 = RELAY [package=relay-t9a-2]
  R2 = Resistor [tolerance=±5% power=0.25 resistance=2k package=THT]
  Heater1 = Camdenboss CTB0158-2 [part_number=CTB0158-2 package=THT]
  D2 = Zener Diode [part_number=30SQ050 breakdown_voltage=3.6V package="300 mil [THT]"]
  D3 = Zener Diode [part_number=30SQ050 breakdown_voltage=3.6V package="300 mil [THT]"]
  Heater2 = Camdenboss CTB0158-2 [part_number=CTB0158-2 package=THT]
  Q2 = Basic FET N-Channel [package="DPak [SMD]"]
  R3 = Resistor [tolerance=±5% power=0.25 resistance=10k package=THT]
  R4 = Resistor [tolerance=±5% power=0.25 resistance=2k package=THT]
  M2 = RioRand LM2596 [part_number=3.3V]
  S1 = Round Pushbutton  # not connected
  C1 = Capacitor [part_number=100nF package=cap-pth-small-kit]  # not connected
  DHT1 = DHT22 Humidity and Temperature Sensor  # not connected
  DC2 = DC_DC_XL4016 [part_number=19V package=board_screw]  # not connected

nets:
  N1: Mod1.SDA, WeMos_D1_Mini1.D2, M1.SDA
  N2: Mod1.SCL, WeMos_D1_Mini1.D1, M1.SCL
  VCC: Mod1.VCC, WeMos_D1_Mini1.3V3, M1.VS, M2.Pin_3
  GND: Mod1.GND, WeMos_D1_Mini1.G, ChargePort.pin1, M1.GND, Q1.source, R1.Pin_1, U4.COIL1, Q2.source, R3.Pin_1, M2.Pin_2, M2.Pin_4
  N3: U3.+, M1.VPU, M1.VN1-, M2.Pin_1
  GND_2: U3.-
  N4: ChargePort.pin2, D1.anode
  N5: M1.VN3+, M1.VN2+, U4.NO, U5.NO
  N6: M1.VN3-, D3.anode
  N7: M1.VN2-, D2.anode
  N8: M1.VN1+, U5.MAIN
  N9: Q1.Gate, R1.Pin_0, R2.Pin_1
  N10: Q1.drain, Heater1.pin2
  N11: D1.cathode, U4.MAIN
  N12: Heater1.pin1, D2.cathode
  N13: D3.cathode, Heater2.pin1
  N14: Heater2.pin2, Q2.drain
  N15: Q2.Gate, R3.Pin_0, R4.Pin_1

custom parts:
  OLED Mono 0.56 inch blue or white: OLED, I2C 3.3V - 5V Blue and White text versions
  INA3221 Triple Channel Current/Voltage Monitor Module: INA3221 Triple Channel Current/Voltage Monitor Module Links: INA3221 product information
